# Fritzing sketch fechadura+NodeMcu (saved by Fritzing 0.9.3b)
breadboards: 2

parts:
  R1 = Resistor [tolerance=±5% resistance=220 package=THT]
  U1 = ESP8266 NodeMCU LoLin base
  LED1 = LED - 5mm [color="Red (633nm)" package="5 mm [THT]"]
  KY-1 = Keyes Relay [package=THT]
  Power_plug1 = Power plug
  L1 = Solenoid
  S1 = Pushbutton [package="[THT]"]
  R2 = Resistor [tolerance=±5% resistance=220 package=THT]
  Componente1 = Arduino Leonardo (Rev3b)
  LED2 = LED - 5mm [color="Red (633nm)" package="5 mm [THT]"]
  R3 = Resistor [tolerance=±5% resistance=220 package=THT]
  KY-2 = Keyes Relay [package=THT]
  Power_plug2 = Power plug
  L2 = Solenoid

nets:
  N1: R1.Pin_0, LED1.anode, KY-1.signal
  N2: R1.Pin_1, U1.D7-0, U1.D7-2
  N3: U1.GND1-3, U1.GND2-0, LED1.cathode, KY-1.ground
  N4: U1.3V4, KY-1.power
  N5: KY-1.NC, Power_plug1.VCC, L1.pin2
  N6: KY-1.C, Power_plug1.GND, L1.pin1
  N7: S1.Pin_1, S1.Pin_2, R2.Pin_0, Componente1.D8/A8
  N8: S1.Pin_3, S1.Pin_4, Componente1.5V, KY-2.power
  N9: R2.Pin_1, Componente1.GND, LED2.cathode, KY-2.ground
  N10: Componente1.D7, R3.Pin_1
  N11: LED2.anode, R3.Pin_0, KY-2.signal
  N12: KY-2.NC, Power_plug2.VCC, L2.pin2
  N13: KY-2.C, Power_plug2.GND, L2.pin1

notes:
  FONTE 12V DC ->
  FECHADURA
  ELETRICA
  FONTE 12V
  DC

custom parts:
  ESP8266 NodeMCU LoLin base: ESP8266 based NodeMCU Base
  Keyes Relay: The Keyes 5V relay module is suitable for SCM development, home appliance control. It uses a 5V~12V TIL control signal which can control DC / AC signal.
